// Digital circuit part_c.dig as structural Verilog
module part_c (
  input  in_0,
  input  in_1,
  input  in_2,
  output out_0
);

  wire nfet_6_d, nfet_7_d, nfet_16_s, nfet_17_s, pfet_1_d, pfet_2_d, pfet_3_d, pfet_4_d, pfet_5_d, pfet_6_d,
       pfet_7_d, pfet_8_d, pfet_10_d, pfet_11_d, pfet_13_d, pfet_14_d, pfet_15_d, pfet_16_d;

  PFET pfet_1 (.G(in_1), .S(1'b1), .D(pfet_1_d));
  NFET nfet_1 (.G(in_1), .D(pfet_1_d), .S(1'b0));
  PFET pfet_2 (.G(in_0), .S(1'b1), .D(pfet_2_d));
  NFET nfet_2 (.G(in_0), .D(pfet_2_d), .S(1'b0));
  PFET pfet_3 (.G(in_2), .S(1'b1), .D(pfet_3_d));
  NFET nfet_3 (.G(in_2), .D(pfet_3_d), .S(1'b0));
  PFET pfet_4 (.G(in_0), .S(1'b1), .D(pfet_4_d));
  PFET pfet_5 (.G(in_1), .S(pfet_4_d), .D(pfet_5_d));
  PFET pfet_6 (.G(pfet_3_d), .S(pfet_5_d), .D(pfet_6_d));
  NFET nfet_4 (.G(in_0), .D(pfet_6_d), .S(1'b0));
  NFET nfet_5 (.G(in_1), .D(pfet_6_d), .S(1'b0));
  NFET nfet_6 (.G(in_0), .D(nfet_6_d), .S(1'b0));
  NFET nfet_7 (.G(pfet_2_d), .D(nfet_7_d), .S(1'b0));
  NFET nfet_8 (.G(pfet_3_d), .D(pfet_6_d), .S(1'b0));
  PFET pfet_7 (.G(in_0), .S(1'b1), .D(pfet_7_d));
  PFET pfet_8 (.G(pfet_1_d), .S(pfet_7_d), .D(pfet_8_d));
  PFET pfet_9 (.G(pfet_3_d), .S(pfet_8_d), .D(nfet_6_d));
  NFET nfet_9 (.G(pfet_1_d), .D(nfet_6_d), .S(1'b0));
  NFET nfet_10 (.G(pfet_3_d), .D(nfet_6_d), .S(1'b0));
  PFET pfet_10 (.G(pfet_2_d), .S(1'b1), .D(pfet_10_d));
  PFET pfet_11 (.G(pfet_1_d), .S(pfet_10_d), .D(pfet_11_d));
  PFET pfet_12 (.G(in_2), .S(pfet_11_d), .D(nfet_7_d));
  NFET nfet_11 (.G(pfet_1_d), .D(nfet_7_d), .S(1'b0));
  PFET pfet_13 (.G(pfet_6_d), .S(1'b1), .D(pfet_13_d));
  NFET nfet_12 (.G(pfet_6_d), .D(pfet_13_d), .S(1'b0));
  PFET pfet_14 (.G(nfet_6_d), .S(1'b1), .D(pfet_14_d));
  NFET nfet_13 (.G(nfet_6_d), .D(pfet_14_d), .S(1'b0));
  NFET nfet_14 (.G(in_2), .D(nfet_7_d), .S(1'b0));
  PFET pfet_15 (.G(nfet_7_d), .S(1'b1), .D(pfet_15_d));
  NFET nfet_15 (.G(nfet_7_d), .D(pfet_15_d), .S(1'b0));
  PFET pfet_16 (.G(pfet_13_d), .S(1'b1), .D(pfet_16_d));
  PFET pfet_17 (.G(pfet_14_d), .S(1'b1), .D(pfet_16_d));
  NFET nfet_16 (.G(pfet_13_d), .D(pfet_16_d), .S(nfet_16_s));
  NFET nfet_17 (.G(pfet_14_d), .D(nfet_16_s), .S(nfet_17_s));
  NFET nfet_18 (.G(pfet_15_d), .D(nfet_17_s), .S(1'b0));
  PFET pfet_18 (.G(pfet_15_d), .S(1'b1), .D(pfet_16_d));
  PFET pfet_19 (.G(pfet_16_d), .S(1'b1), .D(out_0));
  NFET nfet_19 (.G(pfet_16_d), .D(out_0), .S(1'b0));
endmodule
