// Digital circuit lab2_part2.dig as structural Verilog
module lab2_part2 (
  input  in0,
  input  in1,
  input  in2,
  input  in3,
  input  in_21,
  output seg_a,
  output seg_f,
  output seg_b,
  output seg_g,
  output seg_e,
  output seg_c,
  output seg_d,
  output seg_dp,
  output sign_a,
  output sign_f,
  output sign_b,
  output sign_g,
  output sign_e,
  output sign_c,
  output sign_d,
  output sign_dp
);

  wire and_2_out, and_3_out, and_4_out, and_5_out, and_6_out, and_7_out, and_8_out, and_9_out, and_10_out,
       and_11_out, or_1_out, or_2_out, or_3_out, or_5_out, or_8_out, or_9_out, or_10_out, or_11_out,
       or_12_out, or_13_out, or_14_out, or_15_out, or_16_out, or_17_out, or_18_out, or_19_out;

  or or_1 (or_1_out, ~in0, ~in1, in2, ~in3);  // Or
  or or_2 (or_2_out, in0, ~in1, in2, ~in3);  // Or
  and and_1 (seg_b, or_5_out, or_3_out, or_2_out, or_1_out);
  and and_2 (and_2_out, ~in0, ~in2);  // And
  or or_3 (or_3_out, in0, ~in1, ~in2, in3);  // Or
  or or_4 (seg_e, and_3_out, and_2_out);
  and and_3 (and_3_out, ~in0, in1);  // And
  or or_5 (or_5_out, ~in0, in1, ~in2, in3);  // Or
  Seven_Seg seven_seg_1 (.a(in_21), .b(in_21), .c(in_21), .d(in_21), .e(in_21), .f(in_21), .g(in3), .dp(in_21));
  and and_4 (and_4_out, ~in0, in3);  // And
  Seven_Seg seven_seg_2 (.a(seg_a), .b(seg_b), .c(seg_c), .d(seg_d), .e(seg_e), .f(seg_f), .g(seg_g), .dp(in_21));
  and and_5 (and_5_out, ~in0, in1);  // And
  or or_6 (seg_g, and_7_out, and_6_out, and_5_out, and_4_out);
  and and_6 (and_6_out, ~in1, in2);  // And
  and and_7 (and_7_out, in1, ~in2);  // And
  and and_8 (and_8_out, in1, ~in2, in3);  // And
  and and_9 (and_9_out, ~in0, in2, ~in3);  // And
  and and_10 (and_10_out, ~in1, in2, ~in3);  // And
  or or_7 (seg_f, and_11_out, and_10_out, and_9_out, and_8_out);
  and and_11 (and_11_out, ~in0, ~in1);  // And
  or or_8 (or_8_out, ~in0, ~in1, ~in2, ~in3);  // Or
  or or_9 (or_9_out, ~in0, ~in1, ~in2, ~in3);  // Or
  or or_10 (or_10_out, in0, in1, ~in2, ~in3);  // Or
  or or_11 (or_11_out, in0, in1, ~in2, ~in3);  // Or
  or or_12 (or_12_out, ~in0, in1, in2, ~in3);  // Or
  or or_13 (or_13_out, in0, ~in1, ~in2, ~in3);  // Or
  and and_12 (seg_a, or_18_out, or_14_out, or_11_out, or_9_out);
  and and_13 (seg_c, or_17_out, or_13_out);
  or or_14 (or_14_out, in0, in1, ~in2, in3);  // Or
  or or_15 (or_15_out, ~in0, ~in1, ~in2, in3);  // Or
  and and_14 (seg_d, or_19_out, or_16_out, or_15_out, or_12_out, or_10_out, or_8_out);
  or or_16 (or_16_out, in0, in1, ~in2, in3);  // Or
  or or_17 (or_17_out, in0, ~in1, in2, in3);  // Or
  or or_18 (or_18_out, ~in0, in1, in2, in3);  // Or
  or or_19 (or_19_out, ~in0, in1, in2, in3);  // Or

  assign seg_dp = in_21;
  assign sign_a = in_21;
  assign sign_b = in_21;
  assign sign_c = in_21;
  assign sign_d = in_21;
  assign sign_dp = in_21;
  assign sign_e = in_21;
  assign sign_f = in_21;
  assign sign_g = in3;

  // Notes on the sheet:
  //   Interface (do not edit the content inside this box)
  //   Outputs:
  //   Inputs
  //   Sign
  //   Decimal Number
endmodule

/* Test case:
in3 in2 in1 in0  sign_a sign_b sign_c sign_d sign_e sign_f sign_g  seg_a seg_b seg_c seg_d seg_e seg_f seg_g
 0   0   0   0    0      0      0      0      0      0      0       1     1     1     1     1     1     0
*/
